// Logisim project assign1bonus.circ as structural Verilog: 1 circuit, main circuit main
module main (
  input  x,
  input  y,
  input  w,
  input  z
);

  wire A, B, button_1_out, C, D, E, F, G, not_1_out, not_2_out, not_3_out, not_4_out, not_5_out, not_6_out,
       not_7_out, not_8_out, not_9_out, not_10_out, not_11_out, not_12_out, not_13_out, not_14_out,
       not_15_out, not_16_out, not_17_out, not_18_out, not_19_out, not_20_out, not_21_out, not_22_out,
       not_23_out, not_24_out, not_25_out, not_26_out, not_27_out, not_28_out, not_29_out, not_30_out,
       not_31_out, not_32_out, not_33_out, not_34_out, not_35_out, not_36_out, not_37_out, not_38_out,
       not_39_out, not_40_out, not_41_out, not_42_out, not_43_out, not_44_out, not_45_out, w_prime_z_out,
       w_prime_z_prime_out, wz_prime_2_out, wz_prime_out, x_prime_w_out, x_prime_w_prime_out,
       x_prime_w_prime_z_prime_out, x_prime_wz_out, x_prime_y_out, x_prime_y_prime_out,
       x_prime_y_prime_z_prime_2_out, x_prime_y_prime_z_prime_out, x_prime_yw_prime_2_out,
       x_prime_yw_prime_out, x_prime_yz_out, x_prime_z_out, xw_2_out, xw_out, xw_prime_out, xw_prime_z_out,
       xy_out, xy_prime_2_out, xy_prime_3_out, xy_prime_out, xy_prime_w_prime_out, xz_out, xz_prime_2_out,
       xz_prime_out, y_prime_w_out, y_prime_wz_out, y_prime_z_prime_2_out, y_prime_z_prime_out, yw_out,
       yw_prime_z_out, ywz_prime_2_out, ywz_prime_out;
  wire [3:0] counter_1_q;

  not not_1 (not_1_out, x);
  not not_2 (not_2_out, z);
  not not_3 (not_3_out, y);
  not not_4 (not_4_out, z);
  not not_5 (not_5_out, x);
  not not_6 (not_6_out, y);
  not not_7 (not_7_out, w);
  not not_8 (not_8_out, x);
  not not_9 (not_9_out, y);
  not not_10 (not_10_out, y);
  not not_11 (not_11_out, z);
  not not_12 (not_12_out, w);
  not not_13 (not_13_out, x);
  not not_14 (not_14_out, w);
  not not_15 (not_15_out, z);
  not not_16 (not_16_out, x);
  not not_17 (not_17_out, w);
  not not_18 (not_18_out, x);
  not not_19 (not_19_out, y);
  not not_20 (not_20_out, x);
  not not_21 (not_21_out, w);
  not not_22 (not_22_out, x);
  not not_23 (not_23_out, w);
  not not_24 (not_24_out, w);
  not not_25 (not_25_out, z);
  not not_26 (not_26_out, x);
  not not_27 (not_27_out, y);
  not not_28 (not_28_out, z);
  not not_29 (not_29_out, y);
  not not_30 (not_30_out, z);
  not not_31 (not_31_out, x);
  not not_32 (not_32_out, y);
  not not_33 (not_33_out, z);
  not not_34 (not_34_out, z);
  not not_35 (not_35_out, y);
  not not_36 (not_36_out, w);
  not not_37 (not_37_out, z);
  not not_38 (not_38_out, x);
  not not_39 (not_39_out, w);
  not not_40 (not_40_out, z);
  not not_41 (not_41_out, z);
  not not_42 (not_42_out, y);
  not not_43 (not_43_out, y);
  not not_44 (not_44_out, x);
  not not_45 (not_45_out, w);
  and x_prime_w (x_prime_w_out, not_1_out, w);
  and xz_prime (xz_prime_out, x, not_2_out);
  and y_prime_z_prime (y_prime_z_prime_out, not_3_out, not_4_out);
  and yw (yw_out, y, w);
  and x_prime_yz (x_prime_yz_out, not_5_out, y, z);
  and xy_prime_w_prime (xy_prime_w_prime_out, x, not_6_out, not_7_out);
  and x_prime_y_prime (x_prime_y_prime_out, not_8_out, not_9_out);
  and y_prime_z_prime_2 (y_prime_z_prime_2_out, not_10_out, not_11_out);
  and xw_prime_z (xw_prime_z_out, x, not_12_out, z);
  and x_prime_w_prime_z_prime (x_prime_w_prime_z_prime_out, not_13_out, not_14_out, not_15_out);
  and x_prime_wz (x_prime_wz_out, not_16_out, w, z);
  and w_prime_z (w_prime_z_out, not_17_out, z);
  and x_prime_y (x_prime_y_out, not_18_out, y);
  and xy_prime (xy_prime_out, x, not_19_out);
  and x_prime_w_prime (x_prime_w_prime_out, not_20_out, not_21_out);
  and x_prime_z (x_prime_z_out, not_22_out, z);
  and xw_prime (xw_prime_out, x, not_23_out);
  and yw_prime_z (yw_prime_z_out, y, not_24_out, z);
  and ywz_prime (ywz_prime_out, y, w, not_25_out);
  and x_prime_y_prime_z_prime (x_prime_y_prime_z_prime_out, not_26_out, not_27_out, not_28_out);
  and y_prime_wz (y_prime_wz_out, not_29_out, w, z);
  and wz_prime (wz_prime_out, w, not_30_out);
  and xy (xy_out, x, y);
  and x_prime_y_prime_z_prime_2 (x_prime_y_prime_z_prime_2_out, not_31_out, not_32_out, not_33_out);
  and xz_prime_2 (xz_prime_2_out, x, not_34_out);
  and xw (xw_out, x, w);
  and xy_prime_2 (xy_prime_2_out, x, not_35_out);
  and w_prime_z_prime (w_prime_z_prime_out, not_36_out, not_37_out);
  and xw_2 (xw_2_out, x, w);
  and x_prime_yw_prime (x_prime_yw_prime_out, not_38_out, y, not_39_out);
  and ywz_prime_2 (ywz_prime_2_out, y, w, not_40_out);
  and wz_prime_2 (wz_prime_2_out, w, not_41_out);
  and xy_prime_3 (xy_prime_3_out, x, not_42_out);
  and xz (xz_out, x, z);
  and y_prime_w (y_prime_w_out, not_43_out, w);
  and x_prime_yw_prime_2 (x_prime_yw_prime_2_out, not_44_out, y, not_45_out);
  _7_Segment_Display u_7_segment_display_1 (.g(G), .f(F), .a(A), .b(B), .e(E), .d(D), .c(C));  // open: dp
  or or_1 (B, x_prime_y_prime_out, y_prime_z_prime_2_out, xw_prime_z_out, x_prime_w_prime_z_prime_out, x_prime_wz_out);
  or or_2 (A, x_prime_w_out, xz_prime_out, y_prime_z_prime_out, yw_out, x_prime_yz_out, xy_prime_w_prime_out);
  or or_3 (C, w_prime_z_out, x_prime_y_out, xy_prime_out, x_prime_w_prime_out, x_prime_z_out);
  or or_4 (D, xw_prime_out, yw_prime_z_out, ywz_prime_out, x_prime_y_prime_z_prime_out, y_prime_wz_out);
  or or_5 (E, wz_prime_out, xy_out, x_prime_y_prime_z_prime_2_out, xz_prime_2_out, xw_out);
  or or_6 (F, xy_prime_2_out, w_prime_z_prime_out, xw_2_out, x_prime_yw_prime_out, ywz_prime_2_out);
  or or_7 (G, wz_prime_2_out, xy_prime_3_out, xz_out, y_prime_w_out, x_prime_yw_prime_2_out);
  Counter #(.width(4), .max('hf)) counter_1 (.Q(counter_1_q), .clk(button_1_out));  // open: load, D, count, carry, clr
  Button button_1 (.out(button_1_out));

  // Notes on the sheet:
  //   BONUS
endmodule
