// Logisim project assign2.circ as structural Verilog: 1 circuit, main circuit main
// B
module main (
  input  En,
  input  D
);

  wire A, and_1_out, and_2_out, and_3_out, and_4_out, and_5_out, and_6_out, and_7_out, and_8_out, and_9_out,
       and_10_out, and_11_out, and_12_out, and_13_out, and_14_out, and_15_out, and_16_out, B, C, clock_1_out,
       not_1_out, not_2_out, not_3_out, not_4_out, not_5_out, not_6_out, not_7_out, not_8_out, not_9_out,
       not_10_out, not_11_out, not_12_out, not_13_out, not_14_out, not_15_out, not_16_out, not_17_out,
       not_18_out, not_19_out, not_20_out, not_21_out, not_22_out, not_23_out, not_24_out, or_1_out,
       or_2_out, or_3_out, or_4_out, or_5_out, or_6_out;

  not not_1 (not_1_out, B);
  not not_2 (not_2_out, C);
  not not_3 (not_3_out, C);
  not not_4 (not_4_out, D);
  not not_5 (not_5_out, B);
  not not_6 (not_6_out, C);
  not not_7 (not_7_out, D);
  not not_8 (not_8_out, C);
  not not_9 (not_9_out, A);
  not not_10 (not_10_out, D);
  not not_11 (not_11_out, A);
  not not_12 (not_12_out, D);
  not not_13 (not_13_out, A);
  not not_14 (not_14_out, B);
  not not_15 (not_15_out, D);
  not not_16 (not_16_out, A);
  not not_17 (not_17_out, B);
  not not_18 (not_18_out, D);
  not not_19 (not_19_out, A);
  not not_20 (not_20_out, B);
  not not_21 (not_21_out, A);
  not not_22 (not_22_out, D);
  not not_23 (not_23_out, B);
  not not_24 (not_24_out, D);
  and and_1 (and_1_out, not_1_out, not_2_out, En, D);
  and and_2 (and_2_out, B, not_3_out, En, not_4_out);
  and and_3 (and_3_out, not_5_out, not_6_out, En, not_7_out);
  and and_4 (and_4_out, B, not_8_out, En, D);
  and and_5 (and_5_out, not_9_out, C, En, not_10_out);
  and and_6 (and_6_out, A, C, En, D);
  and and_7 (and_7_out, not_11_out, C, En, D);
  and and_8 (and_8_out, A, C, En, not_12_out);
  and and_9 (and_9_out, not_13_out, not_14_out, En, not_15_out);
  and and_10 (and_10_out, not_16_out, B, En, D);
  and and_11 (and_11_out, A, not_17_out, En, D);
  and and_12 (and_12_out, A, B, En, not_18_out);
  and and_13 (and_13_out, not_19_out, not_20_out, En, D);
  and and_14 (and_14_out, not_21_out, B, En, not_22_out);
  and and_15 (and_15_out, A, not_23_out, En, not_24_out);
  and and_16 (and_16_out, A, B, En, D);
  LED led_1 (.in(A));
  or or_1 (or_1_out, and_1_out, and_2_out);
  or or_2 (or_2_out, and_3_out, and_4_out);
  or or_3 (or_3_out, and_5_out, and_6_out);
  or or_4 (or_4_out, and_7_out, and_8_out);
  or or_5 (or_5_out, and_9_out, and_10_out, and_11_out, and_12_out);
  or or_6 (or_6_out, and_13_out, and_14_out, and_15_out, and_16_out);
  LED led_2 (.in(B));
  Clock clock_1 (.out(clock_1_out));
  LED led_3 (.in(C));
  J_K_Flip_Flop j_k_ff_1 (.J(or_1_out), .clk(clock_1_out), .K(or_2_out), .Q(A));  // open: Qn, preset, en, reset
  J_K_Flip_Flop j_k_ff_2 (.J(or_3_out), .clk(clock_1_out), .K(or_4_out), .Q(B));  // open: Qn, preset, en, reset
  J_K_Flip_Flop j_k_ff_3 (.J(or_5_out), .clk(clock_1_out), .K(or_6_out), .Q(C));  // open: Qn, preset, en, reset

  // Notes on the sheet:
  //   Steven Canon-Almagro
  //   10155792
endmodule
