// Logisim project assign2bonus.circ as structural Verilog: 1 circuit, main circuit main
module main (
  input  En,
  input  D
);

  wire A, and_1_out, and_2_out, and_3_out, and_4_out, and_5_out, and_6_out, and_7_out, and_8_out, and_9_out,
       and_10_out, and_11_out, and_12_out, and_13_out, and_14_out, and_15_out, and_16_out, B, C, clock_1_out,
       not_1_out, not_2_out, not_3_out, not_4_out, not_5_out, not_6_out, not_7_out, not_8_out, not_9_out,
       not_10_out, not_11_out, not_12_out, not_13_out, not_14_out, not_15_out, not_16_out, not_17_out,
       not_18_out, not_19_out, not_20_out, not_21_out, not_22_out, not_23_out, not_24_out, not_25_out,
       not_26_out, not_27_out, not_28_out, not_29_out, not_30_out, not_31_out, not_32_out, or_1_out,
       or_2_out, or_3_out;

  LED led_1 (.in(A));
  LED led_2 (.in(B));
  LED led_3 (.in(C));
  not not_1 (not_1_out, A);
  not not_2 (not_2_out, B);
  not not_3 (not_3_out, C);
  not not_4 (not_4_out, A);
  not not_5 (not_5_out, C);
  not not_6 (not_6_out, D);
  not not_7 (not_7_out, B);
  not not_8 (not_8_out, C);
  not not_9 (not_9_out, D);
  not not_10 (not_10_out, C);
  not not_11 (not_11_out, A);
  not not_12 (not_12_out, B);
  not not_13 (not_13_out, D);
  not not_14 (not_14_out, A);
  not not_15 (not_15_out, B);
  not not_16 (not_16_out, D);
  not not_17 (not_17_out, A);
  not not_18 (not_18_out, B);
  not not_19 (not_19_out, C);
  not not_20 (not_20_out, D);
  not not_21 (not_21_out, A);
  not not_22 (not_22_out, B);
  not not_23 (not_23_out, A);
  not not_24 (not_24_out, C);
  not not_25 (not_25_out, A);
  not not_26 (not_26_out, D);
  not not_27 (not_27_out, B);
  not not_28 (not_28_out, C);
  not not_29 (not_29_out, B);
  not not_30 (not_30_out, D);
  not not_31 (not_31_out, C);
  not not_32 (not_32_out, D);
  and and_1 (and_1_out, not_1_out, not_2_out, not_3_out, En, D);
  and and_2 (and_2_out, not_4_out, B, not_5_out, En, not_6_out);
  and and_3 (and_3_out, A, not_7_out, not_8_out, En, not_9_out);
  and and_4 (and_4_out, A, B, not_10_out, En, D);
  and and_5 (and_5_out, not_11_out, not_12_out, C, En, not_13_out);
  and and_6 (and_6_out, not_14_out, B, C, En, D);
  and and_7 (and_7_out, A, not_15_out, C, En, D);
  and and_8 (and_8_out, A, B, C, En, not_16_out);
  and and_9 (and_9_out, not_17_out, not_18_out, not_19_out, En, not_20_out);
  and and_10 (and_10_out, not_21_out, not_22_out, C, En, D);
  and and_11 (and_11_out, not_23_out, B, not_24_out, En, D);
  and and_12 (and_12_out, not_25_out, B, C, En, not_26_out);
  and and_13 (and_13_out, A, not_27_out, not_28_out, En, D);
  and and_14 (and_14_out, A, not_29_out, C, En, not_30_out);
  and and_15 (and_15_out, A, B, C, En, D);
  and and_16 (and_16_out, A, B, not_31_out, En, not_32_out);
  or or_1 (or_1_out, and_1_out, and_2_out, and_3_out, and_4_out);
  or or_2 (or_2_out, and_5_out, and_6_out, and_7_out, and_8_out);
  or or_3 (or_3_out, and_9_out, and_10_out, and_11_out, and_12_out, and_13_out, and_14_out, and_15_out, and_16_out);
  Clock clock_1 (.out(clock_1_out));
  T_Flip_Flop t_ff_1 (.clk(clock_1_out), .T(or_1_out), .Q(A));  // open: Qn, preset, reset, en
  T_Flip_Flop t_ff_2 (.clk(clock_1_out), .T(or_2_out), .Q(B));  // open: Qn, preset, reset, en
  T_Flip_Flop t_ff_3 (.clk(clock_1_out), .T(or_3_out), .Q(C));  // open: Qn, preset, reset, en

  // Notes on the sheet:
  //   Steven Canon-Almagro
  //   10155792
endmodule
